# Fritzing sketch 555-stripboard (saved by Fritzing 0.9.3b)
stripboards: 1

parts:
  U1 = 555 Timer [package="DIP8 [THT]"]
  J1 = Screw terminal - 2 pins [package=THT]
  R1 = Resistor [tolerance=±5% resistance=220k package=THT]
  R2 = Resistor [tolerance=±5% resistance=33k package=THT]
  C2 = Ceramic Capacitor [capacitance=100nF package="100 mil [THT, multilayer]"]
  C3 = Electrolytic Capacitor [capacitance=1µF package="100 mil [THT, electrolytic]"]
  LED1 = LED - 5mm [color="Red (633nm)" package="5 mm [THT]"]
  J2 = female pin header, 2 pins [form="♀ (female)"]

nets:
  N1: U1.Pin_1, J1.pin2, R2.Pin_0, C2.1, C3.+, LED1.cathode, J2.pin1
  N2: U1.Pin_2, U1.Pin_6, R1.Pin_1, R2.Pin_1
  N3: U1.Pin_3, LED1.anode, J2.pin2
  N4: U1.Pin_4, J1.pin1, R1.Pin_0
  N5: U1.Pin_5, C2.0
