# Fritzing sketch 555 (saved by Fritzing 0.9.3b)
breadboards: 1

parts:
  U1 = 555 Timer [package="DIP8 [THT]"]
  R1 = Resistor [tolerance=±5% resistance=330k package=THT]
  C1 = Ceramic Capacitor [capacitance=10nF package="100 mil [THT, multilayer]"]
  R2 = Resistor [tolerance=±5% resistance=220k package=THT]
  C2 = Electrolytic Capacitor [capacitance=1µF package="100 mil [THT, electrolytic]"]

nets:
  GND: U1.Pin_1, C1.1, C2.-
  N1: U1.Pin_2, U1.Pin_6, R1.Pin_0, R2.Pin_0, C2.+
  N2: U1.Pin_3, R1.Pin_1
  5V: U1.Pin_4, U1.Pin_8, R2.Pin_1
  N3: U1.Pin_5, C1.0
